# Fritzing sketch PCB editable file fritzing (saved by Fritzing 1.0.4)
circuit board: 9.7cm x 8.2cm

parts:
  ARDUINO_NANO = Arduino Nano (Rev3.0) (ICSP)
  R1 = Resistor [tolerance=±5% resistance=220 power=0.25W package=THT]
  A4988_STEPPER_DRIVER = Pololu A4988 [package=SO16]
  1B_1A = screw terminal, 2 pins
  2A_2B = screw terminal, 2 pins
  POWER_9V-DC = screw terminal, 2 pins
  DOWN = Pushbutton [package="[THT]"]
  RIGHT = Pushbutton [package="[THT]"]
  LEFT = Pushbutton [package="[THT]"]
  UP = Pushbutton [package="[THT]"]
  16X2_LCD = female pin header, 16 pins [form="♀ (female)"]
  R11 = Trimmer Potentiometer [maximum_resistance=10kΩ knob_status=50% power=0.5W package=THT]
  J1 = male pin header, 3 pins [form="♂ (male)"]  # not connected

nets:
  GND: ARDUINO_NANO.GND, A4988_STEPPER_DRIVER.GND, POWER_9V-DC.pin2, DOWN.Pin_3, DOWN.Pin_4, RIGHT.Pin_3, RIGHT.Pin_4, LEFT.Pin_1, LEFT.Pin_2, UP.Pin_1, UP.Pin_2, 16X2_LCD.pin1, 16X2_LCD.pin5, 16X2_LCD.pin16, R11.leg1
  N1: ARDUINO_NANO.D2, 16X2_LCD.pin11
  N2: ARDUINO_NANO.D3, 16X2_LCD.pin12
  N3: ARDUINO_NANO.D4, 16X2_LCD.pin13
  N4: ARDUINO_NANO.D5, 16X2_LCD.pin14
  N5: ARDUINO_NANO.D6, DOWN.Pin_1
  N6: ARDUINO_NANO.D7, A4988_STEPPER_DRIVER.STEP
  N7: ARDUINO_NANO.D8, A4988_STEPPER_DRIVER.DIR
  N8: ARDUINO_NANO.D9, RIGHT.Pin_1
  N9: ARDUINO_NANO.D11/MOSI, 16X2_LCD.pin6
  N10: ARDUINO_NANO.D12/MISO, 16X2_LCD.pin4
  5V: ARDUINO_NANO.5V, R1.Pin_0, A4988_STEPPER_DRIVER.VDD, 16X2_LCD.pin2, R11.leg2
  N11: ARDUINO_NANO.A1, UP.Pin_3
  N12: ARDUINO_NANO.A0, LEFT.Pin_3
  N13: R1.Pin_1, 16X2_LCD.pin15
  N14: A4988_STEPPER_DRIVER.RESET, A4988_STEPPER_DRIVER.SLEEP
  N15: A4988_STEPPER_DRIVER.1B, 1B_1A.pin1
  N16: A4988_STEPPER_DRIVER.1A, 1B_1A.pin2
  N17: A4988_STEPPER_DRIVER.2A, 2A_2B.pin1
  N18: A4988_STEPPER_DRIVER.2B, 2A_2B.pin2
  N19: A4988_STEPPER_DRIVER.VMOT, POWER_9V-DC.pin1
  N20: 16X2_LCD.pin3, R11.wiper

notes:
  +  -
